# Fritzing sketch Robot_v1 (saved by Fritzing 0.9.6b)
breadboards: 2

parts:
  Part1 = Arduino Uno (Rev3)
  Part2 = Arduino Nano (Rev3.0)
  Part5 = NRF24L01+ Breakout Board
  Part6 = Black Joystick KY-023
  IR1 = TSOP312.., 314.. [package=THT]
  M1 = DC Motor
  M2 = DC Motor
  M3 = DC Motor
  M4 = DC Motor
  HC-SR04_Sensor_2 = HC-SR04 Ultrasonic Distance Sensor
  S1 = H-Bridge with L298N
  VCC2 = Battery
  VCC1 = Battery
  VCC3 = Battery

nets (from the breadboard view):
  N1: Part1.D8, S1.IN3
  N2: Part1.D9_PWM, S1.ENB
  N3: Part1.D10_PWM/SS, S1.ENA
  N4: Part1.D11_PWM/MOSI, S1.IN2
  N5: Part1.D12/MISO, S1.IN4
  GND: Part1.GND, IR1.GND, HC-SR04_Sensor_2.GND, S1.GND, VCC2.-
  N6: Part1.D2, IR1.Data
  N7: Part1.D3_PWM, HC-SR04_Sensor_2.ECHO
  N8: Part1.D4, HC-SR04_Sensor_2.TRIG
  N9: Part1.D7, S1.IN1
  5V: Part1.5V, IR1.Vs, HC-SR04_Sensor_2.VCC, S1.5V
  GND_2: Part2.GND, Part5.GND, Part6.GND
  N10: Part2.D7, Part5.CE
  N11: Part2.D8, Part5.CS
  N12: Part2.D11/MOSI, Part5.MOSI
  N13: Part2.D12/MISO, Part5.MISO
  5V_2: Part2.5V, Part6.+5V
  N14: Part2.A1, Part6.VRy
  N15: Part2.A0, Part6.VRx
  3V3: Part2.3V3, Part5.VCC
  N16: Part2.D13/SCK, Part5.SCK
  N17: M1.pin_1, M2.pin_1, S1.M1-02
  N18: M1.pin_2, M2.pin_2, S1.M1-01
  N19: M3.pin_1, M4.pin_1, S1.M2-02
  N20: M3.pin_2, M4.pin_2, S1.M2-01
  N21: S1.12V, VCC1.+
  N22: VCC2.+, VCC3.-
  N23: VCC1.-, VCC3.+

notes:
  This ultasonc sensor will be placed on the front of the cart to enssure that collisions do not occur
  This will be the remote control for the robot if I revive an rf module on time

custom parts:
  Black Joystick KY-023: Description: The joystick is a combination of 2 analoog potentiometer and a digital switch. Arduino GND --> Module pin - Arduino +5V --> Module pin +5V Arduino Analoog 0 --> Module VRx Arduino Analoog 1 --> Module VRy Arduino Digital --> Module SW Dimensions: 1" x 1.25"
  HC-SR04 Ultrasonic Distance Sensor: The HC-SR04 is an ultrasonic distance sensor. It is capable of providing measurement for ranges of 2cm to 400cm. The module operates at 5V.
  H-Bridge with L298N: h-bridge
